# Fritzing sketch HuertoInteligente (saved by Fritzing 0.9.3b)
circuit board: 7.2cm x 7cm
breadboards: 1

parts:
  pot_1 = POT [package=3362u]
  Sensor_de_temperatura = DHT22 Humidity and Temperature Sensor
  Sensor_de_humedad = SparkFun Soil Moisture Sensor [part_number=SEN-13322]
  Servo_1 = Basic Servo
  LCD_1 = LCD-16X2 [package=lcd-16x2_noholes]
  R1 = Resistor [tolerance=±5% resistance=47k package=THT]
  Placa_Principal = Arduino Uno (Rev3)

nets:
  GND: pot_1.E, Sensor_de_temperatura.GND, Sensor_de_humedad.GND, Servo_1.gnd, LCD_1.VSS, LCD_1.R_W, LCD_1.K, Placa_Principal.GND
  N1: pot_1.S, LCD_1.VO
  5V: pot_1.A, Sensor_de_temperatura.VDD, Sensor_de_humedad.VCC, Servo_1.vcc, LCD_1.VDD, LCD_1.A, R1.Pin_0, Placa_Principal.5V
  D10: Sensor_de_temperatura.DATA, R1.Pin_1, Placa_Principal.D10_PWM/SS
  D6: Sensor_de_humedad.SIG, Placa_Principal.D6_PWM
  D9: Servo_1.pulse, Placa_Principal.D9_PWM
  D12: LCD_1.RS, Placa_Principal.D12/MISO
  D11: LCD_1.E, Placa_Principal.D11_PWM/MOSI
  D5: LCD_1.DB4, Placa_Principal.D5_PWM
  D4: LCD_1.DB5, Placa_Principal.D4
  D3: LCD_1.DB6, Placa_Principal.D3_PWM
  D2: LCD_1.DB7, Placa_Principal.D2

notes:
  Huerto Inteligente
  @klhernandez42 - Github

custom parts:
  SparkFun Soil Moisture Sensor: The SparkFun Soil Moisture Sensor is a simple breakout for measuring the moisture in soil and similar materials.

// code stored in the sketch: LCD_solo.ino
/* Este código es para probrar el correcto funcionamiento de la LCD de 16x2
 * puedes encontrar el esquematico y mas detalles de como conectarlo en el repositorio de Github: 
 * https://github.com/klhernandez42/HuertoInteligente
 */
#include  <LiquidCrystal.h> //Libreria para LCD (https://www.arduino.cc/en/Reference/LiquidCrystal)

LiquidCrystal  lcd(12, 11, 5, 4, 3, 2); //lcd(rs,enable,d4,d5,d6,d7);
 
void setup()
{
  lcd.begin(16, 2); //dimensiones de la pantalla en este caso LCD de 16x2
  lcd.home();//El mensaje se iniciara en la posición (0,0)
  lcd.print("Hola Mundo");//mensaje a imprimir en primer linea
  lcd.setCursor ( 0, 1 ); //El mensaje se iniciara en la posición (1,0)
  lcd.print("prueba...");//mensaje a imprimir en segunda linea
  delay(1000);
}
 
void loop()
{
  //El efecto que se utiliza es para mover el mensaje de un lado al otro en la LCD
  int i; //Variable para control de ciclos.
 
  // Dezplazando la pantalla a la derecha
  for ( int i = 0; i < 6; i++ ) {
    lcd.scrollDisplayRight();
    delay (1000);
  }
 
  // Dezplazando la pantalla a la izquierda
  for ( int i = 0; i < 6; i++ ) {
    lcd.scrollDisplayLeft();
    delay (1000);
  }
}
